# Fritzing sketch Light_Tower_Panel (saved by Fritzing 0.9.3b)
breadboards: 1

parts:
  White_button = Momentary Switch [package=tactile-pth]
  LED_in_red_button = LED - 5mm [color="Red (633nm)" package="5 mm [THT]"]
  Red_button = Momentary Switch [package=tactile-pth]
  R1 = Resistor [tolerance=±5% resistance=220 package="1206 [SMD]"]
  U1 = mystery part, 3 pins [chip_label=? part_number=PIR]
  U2 = mystery part, 20 pins [chip_label="Raspberry PI GPIO"]

nets:
  N1: White_button.2, U2.pin12
  N2: White_button.4, LED_in_red_button.cathode, Red_button.4, U1.pin2, U2.pin6
  N3: LED_in_red_button.anode, R1.Pin_0
  N4: Red_button.2, U2.pin15
  N5: R1.Pin_1, U2.pin13
  N6: U1.pin1, U2.pin2
  N7: U1.pin3, U2.pin11
